# Fritzing sketch Ventilator-sch (saved by Fritzing 0.9.4)
breadboards: 1

parts:
  R1 = Rotary Potentiometer (Small) [maximum_resistance=50kΩ part_number=SPEED package=THT]
  R2 = Rotary Potentiometer (Small) [maximum_resistance=50kΩ part_number=VOL package=THT]
  R3 = Rotary Potentiometer (Small) [maximum_resistance=50kΩ part_number=BMP package=THT]
  元件1 = Arduino Uno (Rev3)
  Display1 = LCD screen 16x2 IIC [part_number=101290]
  S1 = Round Pushbutton [part_number="RUN SWITCH"]
  S7 = SWITCH-MOMENTARY-2 [part_number="HOME SENER" package=tactile_switch_smd-2]
  M1 = Stepper Motor - Bipolar
  U1 = TB6560
  VCC1 = Battery

nets:
  5V: R1.leg1, R3.leg1, 元件1.5V, Display1.VCC
  N1: R1.wiper, 元件1.A2
  N2: R2.wiper, 元件1.A1
  GND: R2.leg2, R3.leg2, 元件1.GND, Display1.GND, S1.leg1, S7.1, U1.connector7, U1.connector9, U1.connector11
  N3: R3.wiper, 元件1.A0
  N4: 元件1.A4/SDA, Display1.SDA
  N5: 元件1.A5/SCL, Display1.SCL
  N6: 元件1.D2, U1.connector8
  N7: 元件1.D3_PWM, U1.connector6
  N8: 元件1.D4, U1.connector10
  N9: 元件1.D5_PWM, S7.2
  N10: 元件1.D6_PWM, S1.leg0
  N11: M1.A, U1.connector5
  N12: M1.C, U1.connector4
  N13: M1.B, U1.connector3
  N14: M1.D, U1.connector2
  N15: U1.connector0, VCC1.+
  N16: U1.connector1, VCC1.-

custom parts:
  LCD screen 16x2 IIC: LCD screen with HD44780 controller enables showing text, symbols, value or anything else that comes from Croduino/Arduino. It is capable of showing 16 symbols in two lines and therefore can be used in many projects that need to send clearly visible and legible output information.. • Color of symbols: White • Backlight: Blue • Dimensions: 80 x 36 x 12 mm • Screen dimensions: 64.5 x 16 mm •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
